// Logisim project calculator.circ as structural Verilog: 8 circuits, main circuit pro
module pro (
  input  SA,
  input  A2,
  input  A1,
  input  A0,
  input  FA0,
  input  FA1,
  input  in_7,
  input  SB,
  input  B1,
  input  B0,
  input  FB0,
  input  in_12
);

  wire and_1_out, and_2_out, and_3_out, and_4_out, and_5_out, and_6_out, and_7_out, and_8_out, and_9_out,
       and_10_out, and_11_out, and_12_out, and_13_out, and_14_out, and_15_out, bcd_to_decimale_1_a1,
       bcd_to_decimale_1_a2, bcd_to_decimale_1_b1, bcd_to_decimale_1_b2, bcd_to_decimale_1_c1,
       bcd_to_decimale_1_c2, bcd_to_decimale_1_d1, bcd_to_decimale_1_d2, bcd_to_decimale_1_e1,
       bcd_to_decimale_1_e2, bcd_to_decimale_1_f1, bcd_to_decimale_1_f2, bcd_to_decimale_1_g1,
       bcd_to_decimale_1_g2, decimale_1_a, decimale_1_b, decimale_1_c_2, decimale_1_d, decimale_1_e,
       decimale_1_f, decimale_1_g, full_adder_1_carray, full_adder_1_sum, full_adder_2_carray,
       full_adder_2_sum, full_adder_3_carray, full_adder_3_sum, full_adder_4_carray, full_adder_4_sum,
       full_adder_5_carray, full_adder_5_sum, full_adder_6_carray, full_adder_6_sum, full_adder_7_carray,
       full_adder_7_sum, half_adder_1_c, half_adder_1_s, half_adder_2_c, half_adder_2_s, half_adder_3_c,
       half_adder_3_s, nor_1_out, nor_2_out, not_1_out, not_2_out, or_1_out, xor_1_out;

  and and_1 (and_1_out, FA1, FB0);
  and and_2 (and_2_out, FA0, B1);
  and and_3 (and_3_out, A1, B0);
  and and_4 (and_4_out, FB0, A2);
  and and_5 (and_5_out, A0, FB0);
  and and_6 (and_6_out, B0, FA1);
  and and_7 (and_7_out, FA0, FB0);
  and and_8 (and_8_out, B1, A1);
  and and_9 (and_9_out, B1, A2);
  and and_10 (and_10_out, B0, A0);
  and and_11 (and_11_out, A1, FB0);
  and and_12 (and_12_out, FA0, B0);
  and and_13 (and_13_out, A0, B1);
  and and_14 (and_14_out, B1, FA1);
  full_adder full_adder_1 (
    .a(full_adder_5_sum), .b(and_2_out), .c(half_adder_2_c), .sum(full_adder_1_sum),
    .carray(full_adder_1_carray));
  nor nor_1 (nor_1_out, FB0, B0, B1);
  full_adder full_adder_2 (
    .a(and_3_out), .b(and_4_out), .c(full_adder_5_carray), .sum(full_adder_2_sum),
    .carray(full_adder_2_carray));
  full_adder full_adder_3 (
    .a(half_adder_1_c), .b(and_5_out), .c(and_12_out), .sum(full_adder_3_sum), .carray(full_adder_3_carray));
  half_adder half_adder_1 (.a(and_6_out), .b(and_7_out), .s(half_adder_1_s), .c(half_adder_1_c));
  nor nor_2 (nor_2_out, FA1, FA0, A0, A1, A2);
  full_adder full_adder_4 (
    .a(half_adder_3_c), .b(full_adder_6_carray), .c(and_9_out), .sum(full_adder_4_sum),
    .carray(full_adder_4_carray));
  full_adder full_adder_5 (
    .a(and_10_out), .b(and_11_out), .c(full_adder_3_carray), .sum(full_adder_5_sum),
    .carray(full_adder_5_carray));
  and and_15 (and_15_out, A2, B0);
  half_adder half_adder_2 (.a(full_adder_3_sum), .b(and_14_out), .s(half_adder_2_s), .c(half_adder_2_c));
  full_adder full_adder_6 (
    .a(half_adder_3_s), .b(full_adder_7_carray), .c(and_8_out), .sum(full_adder_6_sum),
    .carray(full_adder_6_carray));
  or or_1 (or_1_out, nor_2_out, nor_1_out);
  half_adder half_adder_3 (.a(full_adder_2_carray), .b(and_15_out), .s(half_adder_3_s), .c(half_adder_3_c));
  LED led_1 (.in(or_1_out));
  full_adder full_adder_7 (
    .a(full_adder_2_sum), .b(full_adder_1_carray), .c(and_13_out), .sum(full_adder_7_sum),
    .carray(full_adder_7_carray));
  xor xor_1 (xor_1_out, SA, SB);
  _7_Segment_Display u_7_segment_display_1 (
    .g(bcd_to_decimale_1_g2), .f(bcd_to_decimale_1_f2), .a(bcd_to_decimale_1_a2), .b(bcd_to_decimale_1_b2),
    .e(bcd_to_decimale_1_e2), .d(bcd_to_decimale_1_d2), .c(bcd_to_decimale_1_c2));  // open: dp
  _7_Segment_Display u_7_segment_display_2 (
    .g(bcd_to_decimale_1_g1), .f(bcd_to_decimale_1_f1), .a(bcd_to_decimale_1_a1), .b(bcd_to_decimale_1_b1),
    .e(bcd_to_decimale_1_e1), .d(bcd_to_decimale_1_d1), .c(bcd_to_decimale_1_c1), .dp(not_1_out));
  bcd_to_decimale bcd_to_decimale_1 (
    .in_1(full_adder_1_sum), .in_2(full_adder_7_sum), .in_3(full_adder_6_sum), .in_4(full_adder_4_sum),
    .in_5(full_adder_4_carray), .in_6(in_12), .b1(bcd_to_decimale_1_b1), .a1(bcd_to_decimale_1_a1),
    .f1(bcd_to_decimale_1_f1), .g1(bcd_to_decimale_1_g1), .c1(bcd_to_decimale_1_c1),
    .d1(bcd_to_decimale_1_d1), .e1(bcd_to_decimale_1_e1), .b2(bcd_to_decimale_1_b2),
    .a2(bcd_to_decimale_1_a2), .f2(bcd_to_decimale_1_f2), .g2(bcd_to_decimale_1_g2),
    .c2(bcd_to_decimale_1_c2), .d2(bcd_to_decimale_1_d2), .e2(bcd_to_decimale_1_e2));
  LED led_2 (.in(xor_1_out));
  not not_1 (not_1_out, in_7);
  _7_Segment_Display u_7_segment_display_3 (
    .g(decimale_1_g), .f(decimale_1_f), .a(decimale_1_a), .b(decimale_1_b), .e(decimale_1_e),
    .d(decimale_1_d), .c(decimale_1_c_2));  // open: dp
  decimale decimale_1 (
    .in_1(half_adder_2_s), .in_2(half_adder_1_s), .in_3(and_1_out), .c(not_2_out), .b(decimale_1_b),
    .a(decimale_1_a), .f(decimale_1_f), .g(decimale_1_g), .e(decimale_1_e), .d(decimale_1_d),
    .c_2(decimale_1_c_2));
  not not_2 (not_2_out, in_12);

  // Notes on the sheet:
  //   1
  //   2
  //   4
  //   6
  //   7
  //   8
  //   3
  //   7
  //   zero flage
  //   5
  //   sign
endmodule

module half_adder (
  input  a,
  input  b,
  output s,
  output c
);

  xor xor_1 (s, a, b);
  and and_1 (c, a, b);
endmodule

module full_adder (
  input  a,
  input  b,
  input  c,
  output sum,
  output carray
);

  wire and_1_out, and_2_out, xor_1_out, xor_2_out;

  xor xor_1 (xor_1_out, a, b);
  and and_1 (and_1_out, b, a);
  and and_2 (and_2_out, xor_1_out, c);
  xor xor_2 (xor_2_out, a, b);
  xor xor_3 (sum, xor_2_out, c);
  or or_1 (carray, and_1_out, and_2_out);
endmodule

module decimale (
  input  in_1,
  input  in_2,
  input  in_3,
  input  c,
  output b,
  output a,
  output f,
  output g,
  output e,
  output d,
  output c_2
);

  wire and_1_out, and_2_out, not_1_out, not_2_out, not_3_out, not_4_out, not_5_out, not_6_out, xnor_1_out,
       xor_1_out;

  not not_1 (not_1_out, in_3);
  not not_2 (not_2_out, in_1);
  not not_3 (not_3_out, in_1);
  not not_4 (not_4_out, in_2);
  not not_5 (not_5_out, in_3);
  or or_1 (d, not_5_out, in_1);
  not not_6 (not_6_out, in_3);
  or or_2 (b, in_2, not_2_out);
  xor xor_1 (xor_1_out, in_2, in_3);
  and and_1 (and_1_out, not_3_out, not_4_out, not_1_out);
  or or_3 (a, in_1, not_6_out);
  xnor xnor_1 (xnor_1_out, in_2, in_3);
  and and_2 (and_2_out, in_1, xor_1_out);
  or or_4 (f, in_1, xnor_1_out);
  or or_5 (e, and_2_out, and_1_out);
  or or_6 (g, in_1, in_2);

  assign c_2 = c;

  // Notes on the sheet:
  //   d
  //   b
  //   a
  //   f
  //   g
  //   e
  //   f
  //   b
  //   a
  //   g
endmodule

module r2 (
  input  c2,
  input  c3,
  input  c4,
  input  c5,
  output out_5
);

  wire and_1_out, and_2_out, and_3_out, and_4_out, and_5_out, not_1_out, not_2_out, not_3_out, not_4_out,
       not_5_out, not_6_out, not_7_out;

  not not_1 (not_1_out, c4);
  not not_2 (not_2_out, c2);
  and and_1 (and_1_out, c2, c3, not_1_out);
  not not_3 (not_3_out, c3);
  not not_4 (not_4_out, c2);
  not not_5 (not_5_out, c5);
  not not_6 (not_6_out, c3);
  and and_2 (and_2_out, not_3_out, c5, c2, c4);
  not not_7 (not_7_out, c5);
  and and_3 (and_3_out, not_1_out, not_3_out, not_2_out, c5);
  and and_4 (and_4_out, c2, not_5_out, not_6_out, not_1_out);
  and and_5 (and_5_out, not_7_out, c3, c4, not_4_out);
  or or_1 (out_5, and_4_out, and_3_out, and_2_out, and_5_out, and_1_out);
endmodule

module bcd_to_decimale (
  input  in_1,
  input  in_2,
  input  in_3,
  input  in_4,
  input  in_5,
  input  in_6,
  output b1,
  output a1,
  output f1,
  output g1,
  output c1,
  output d1,
  output e1,
  output b2,
  output a2,
  output f2,
  output g2,
  output c2,
  output d2,
  output e2
);

  wire integer_to_bcd_2_1__4_2, integer_to_bcd_2_1_r1, integer_to_bcd_2_1_r2, integer_to_bcd_2_1_r3,
       integer_to_bcd_2_1_r5, integer_to_bcd_2_1_r6, integer_to_bcd_2_1_r7, integer_to_bcd_2_1_r8;

  integer_to_bcd_2 integer_to_bcd_2_1 (
    ._1(in_1), ._2(in_2), ._3(in_3), ._4(in_4), ._5(in_5), .in_6(in_6), .r1(integer_to_bcd_2_1_r1),
    .r2(integer_to_bcd_2_1_r2), .r5(integer_to_bcd_2_1_r5), .r3(integer_to_bcd_2_1_r3),
    .r6(integer_to_bcd_2_1_r6), ._4_2(integer_to_bcd_2_1__4_2), .r7(integer_to_bcd_2_1_r7),
    .r8(integer_to_bcd_2_1_r8));
  ic_2 ic_2_1 (
    .x(integer_to_bcd_2_1__4_2), .y(integer_to_bcd_2_1_r3), .w(integer_to_bcd_2_1_r2),
    .z(integer_to_bcd_2_1_r1), .a(a1), .b(b1), .c(c1), .d(d1), .e(e1), .f(f1), .g(g1));
  ic_2 ic_2_2 (
    .x(integer_to_bcd_2_1_r8), .y(integer_to_bcd_2_1_r7), .w(integer_to_bcd_2_1_r6),
    .z(integer_to_bcd_2_1_r5), .a(a2), .b(b2), .c(c2), .d(d2), .e(e2), .f(f2), .g(g2));

  // Notes on the sheet:
  //   tens
  //   ones
endmodule

module integer_to_bcd_2 (
  input  _1,
  input  _2,
  input  _3,
  input  _4,
  input  _5,
  input  in_6,
  output r1,
  output r2,
  output r5,
  output r3,
  output r6,
  output _4_2,
  output r7,
  output r8
);

  wire and_1_out, and_2_out, and_3_out, and_4_out, and_5_out, and_6_out, and_7_out, and_8_out, and_9_out,
       and_10_out, and_11_out, not_1_out, not_2_out, not_3_out, not_4_out, not_5_out, not_6_out, not_7_out,
       not_8_out, not_9_out, not_10_out, not_11_out, not_12_out, or_3_out;

  not not_1 (not_1_out, _4);
  not not_2 (not_2_out, _5);
  not not_3 (not_3_out, _3);
  not not_4 (not_4_out, _5);
  not not_5 (not_5_out, _4);
  not not_6 (not_6_out, _3);
  not not_7 (not_7_out, _2);
  not not_8 (not_8_out, _2);
  not not_9 (not_9_out, _3);
  not not_10 (not_10_out, _2);
  and and_1 (and_1_out, not_7_out, _3, _5, _4);
  and and_2 (and_2_out, _3, not_1_out, not_2_out);
  and and_3 (and_3_out, _3, not_2_out, _2);
  not not_11 (not_11_out, _3);
  and and_4 (and_4_out, not_3_out, _5, _4);
  and and_5 (and_5_out, not_4_out, _4, not_9_out, not_10_out);
  and and_6 (and_6_out, _5, not_5_out, not_6_out, _2);
  and and_7 (and_7_out, _5, not_11_out, not_8_out);
  and and_8 (and_8_out, _3, _4, not_2_out);
  and and_9 (and_9_out, _2, _4, not_2_out);
  or or_1 (r3, and_2_out, and_3_out, and_7_out, and_4_out);
  or or_2 (_4_2, and_5_out, and_6_out, and_1_out);
  and and_10 (and_10_out, _4, _3, _2);
  not not_12 (not_12_out, _3);
  or or_3 (or_3_out, _3, _4);
  and and_11 (and_11_out, not_12_out, not_1_out, _5);
  and and_12 (r6, _5, or_3_out);
  r2 r2_1 (.c2(_2), .c3(_3), .c4(_4), .c5(_5), .out_5(r2));
  or or_4 (r5, and_8_out, and_9_out, and_10_out, and_11_out);

  assign r1 = _1;
  assign r7 = in_6;
  assign r8 = in_6;
endmodule

module ic_2 (
  input  x,
  input  y,
  input  w,
  input  z,
  output a,
  output b,
  output c,
  output d,
  output e,
  output f,
  output g
);

  wire and_1_out, and_2_out, and_3_out, and_4_out, and_5_out, and_6_out, and_7_out, and_8_out, and_9_out,
       and_10_out, and_11_out, and_12_out, and_13_out, and_14_out, and_15_out, and_16_out, and_17_out,
       not_1_out, not_2_out, not_3_out, not_4_out, not_5_out, not_6_out, not_7_out, not_8_out, not_9_out,
       not_10_out, not_11_out, not_12_out, not_13_out, not_14_out, not_15_out, not_16_out, not_17_out,
       not_18_out, not_19_out, not_20_out, not_21_out, or_1_out, or_2_out, or_3_out, or_4_out, or_6_out,
       or_8_out, or_9_out, or_10_out, or_11_out, or_14_out, or_15_out;

  not not_1 (not_1_out, y);
  and and_1 (and_1_out, not_1_out, not_2_out);
  not not_2 (not_2_out, z);
  and and_2 (and_2_out, y, z);
  not not_3 (not_3_out, y);
  not not_4 (not_4_out, w);
  and and_3 (and_3_out, not_4_out, not_5_out);
  not not_5 (not_5_out, z);
  not not_6 (not_6_out, w);
  or or_1 (or_1_out, not_6_out, z);
  not not_7 (not_7_out, y);
  and and_4 (and_4_out, not_7_out, not_8_out);
  not not_8 (not_8_out, z);
  not not_9 (not_9_out, y);
  and and_5 (and_5_out, not_9_out, w);
  not not_10 (not_10_out, z);
  and and_6 (and_6_out, y, not_11_out);
  not not_11 (not_11_out, w);
  not not_12 (not_12_out, y);
  and and_7 (and_7_out, not_12_out, not_13_out);
  not not_13 (not_13_out, z);
  and and_8 (and_8_out, w, not_14_out);
  not not_14 (not_14_out, z);
  not not_15 (not_15_out, w);
  and and_9 (and_9_out, not_15_out, not_16_out);
  not not_16 (not_16_out, z);
  and and_10 (and_10_out, y, not_17_out);
  not not_17 (not_17_out, w);
  and and_11 (and_11_out, y, not_18_out);
  not not_18 (not_18_out, z);
  not not_19 (not_19_out, y);
  and and_12 (and_12_out, not_19_out, w);
  and and_13 (and_13_out, y, not_20_out);
  not not_20 (not_20_out, w);
  and and_14 (and_14_out, y, not_21_out);
  not not_21 (not_21_out, z);
  or or_2 (or_2_out, and_1_out, w);
  or or_3 (or_3_out, and_2_out, x);
  or or_4 (or_4_out, not_3_out, and_3_out);
  and and_15 (and_15_out, w, z);
  or or_5 (c, or_1_out, y);
  or or_6 (or_6_out, and_4_out, and_5_out);
  and and_16 (and_16_out, w, not_10_out);
  and and_17 (and_17_out, and_6_out, z);
  or or_7 (e, and_7_out, and_8_out);
  or or_8 (or_8_out, and_9_out, and_10_out);
  or or_9 (or_9_out, and_11_out, x);
  or or_10 (or_10_out, and_12_out, and_13_out);
  or or_11 (or_11_out, and_14_out, x);
  or or_12 (a, or_2_out, or_3_out);
  or or_13 (b, or_4_out, and_15_out);
  or or_14 (or_14_out, or_6_out, and_16_out);
  or or_15 (or_15_out, and_17_out, x);
  or or_16 (f, or_8_out, or_9_out);
  or or_17 (g, or_10_out, or_11_out);
  or or_18 (d, or_14_out, or_15_out);
endmodule
